# Fritzing sketch DeltaReader-fritzing (saved by Fritzing 0.9.5d)
breadboards: 1

parts:
  WeMos_D1_Mini1 = WeMos D1 Mini [part_number=Controller]
  R1 = Resistor [tolerance=±5% resistance=20k package=THT]
  R2 = Resistor [tolerance=±5% resistance=10k package=THT]
  RJ48_Cable = RJ45 Jack [package=rj45-8]
  Display_connector_(future) = female pin header, 4 pins [form="♀ (female)"]
  RS485_to_TTL = IC, DIP package, 8 pins [chip_label=IC]

nets:
  N1: WeMos_D1_Mini1.3V3, Display_connector_(future).pin1
  N2: WeMos_D1_Mini1.5V, RS485_to_TTL.pin1
  N3: WeMos_D1_Mini1.D1, Display_connector_(future).pin3
  N4: WeMos_D1_Mini1.D2, Display_connector_(future).pin4
  N5: WeMos_D1_Mini1.D5, R1.Pin_0, R2.Pin_0
  N6: WeMos_D1_Mini1.D6, RS485_to_TTL.pin2
  N7: WeMos_D1_Mini1.G, R1.Pin_1, Display_connector_(future).pin2, RS485_to_TTL.pin4
  N8: R2.Pin_1, RS485_to_TTL.pin3
  N9: RJ48_Cable.5, RS485_to_TTL.pin8
  N10: RJ48_Cable.6, RS485_to_TTL.pin6
  N11: RJ48_Cable.7, RS485_to_TTL.pin5

notes:
  5v -> 3.3v divider
